// Logisim project Indicador_de_portas.circ as structural Verilog: 1 circuit, main circuit main
module main (
  input  in_1,
  input  in_2,
  input  in_3
);

  wire and_1_out, and_2_out, or_1_out, or_2_out, xor_1_out, xor_2_out;

  or or_1 (or_1_out, in_1, in_2);
  xor xor_1 (xor_1_out, in_1, in_2);
  and and_1 (and_1_out, in_1, in_2);
  and and_2 (and_2_out, in_3, or_1_out);
  xor xor_2 (xor_2_out, xor_1_out, in_3);
  // Probe on or_2_out
  or or_2 (or_2_out, and_1_out, and_2_out);
  // Probe on xor_2_out

  // Other names for the same wires on the sheet: A = in_3; B = in_2; C = in_1
endmodule
